# Fritzing sketch DoorActuator (saved by Fritzing 0.9.3b)
breadboards: 1

parts:
  Part1 = Photon
  DRV_1 = DRV 8825 Stepper Motor Carrier, High Current [part_number="DRV 8825"]
  U1 = HALL-EFFECT [package=sc70]
  C1 = Capacitor Polarized [package=cpol-radial-100uf-25v]
  R1 = Resistor [tolerance=±5% resistance=220 package="0402 [SMD]"]
  S1 = SPST Switch [package=switch-spdt-smd]
  S2 = SPST Switch [package=switch-spdt-smd]
  M1 = Stepper Motor - Bipolar
  VCC1 = 4 x AAA Battery Mount

nets:
  N1: Part1.A5, U1.VCC
  GND: Part1.GND, DRV_1.GROUND_LOG, U1.GND
  N2: Part1.D3, DRV_1.MS2
  N3: Part1.D4, S2.P
  N4: Part1.D5, S1.P
  N5: Part1.D6, U1.OUT
  N6: Part1.3V3, R1.Pin_1
  N7: DRV_1.OUT_2A, M1.C
  N8: DRV_1.OUT_1A, M1.B
  N9: DRV_1.OUT_1B, M1.D
  N10: C1.+, VCC1.+
  N11: C1.-, VCC1.-
  N12: R1.Pin_0, S1.O, S2.O
